# Fritzing sketch Primeiro Esquematico - v0 (saved by Fritzing 0.9.3b)
breadboards: 1

parts:
  U1 = NodeMCU V1.0
  R1 = Photocell (LDR) [package=THT]
  R2 = Resistor [tolerance=±5% resistance=10k package=THT]
  PIR1 = PIR sensor
  R3 = Resistor [tolerance=±5% resistance=220 package=THT]
  LED1 = smd LED [color="Red (633nm)" package="0603 [SMD]"]

nets:
  N1: U1.D1, R3.Pin_0
  N2: U1.D2, PIR1.SIG
  GND: U1.GND, R2.Pin_1, PIR1.GND, R3.Pin_1, LED1.cathode, LED1.anode
  VIN: U1.Vin, R1.pin_0, PIR1.VDD
  N3: U1.A0, R1.pin_1, R2.Pin_0

custom parts:
  NodeMCU V1.0: ESP8266 based NodeMCU
