# Fritzing sketch Primeiro Esquematico - v1 (saved by Fritzing 0.9.3b)
breadboards: 1

parts:
  U1 = NodeMCU V1.0
  R1 = Photocell (LDR) [package=THT]
  R2 = Resistor [tolerance=±5% resistance=10k package=THT]
  PIR1 = PIR sensor
  Componente1 = Jtron 1 Channel Optoisolated Relay Module [package=relay]
  J1 = Screw terminal - 2 pins [package=THT]

nets:
  N1: U1.D1, Componente1.IN1
  N2: U1.D2, PIR1.SIG
  GND: U1.GND, R2.Pin_1, PIR1.GND
  VIN: U1.Vin, R1.pin_0, PIR1.VDD, Componente1.VCC
  N3: U1.A0, R1.pin_1, R2.Pin_0
  N4: Componente1.NO, J1.pin1

notes:
  127 / 220Vac
  Conector - Lampada LED
  Módulo Relay 1 Canal (Utilizado Contato NO)

custom parts:
  NodeMCU V1.0: ESP8266 based NodeMCU
