# Fritzing sketch Primeiro Esquematico - v2 (saved by Fritzing 0.9.2b)
breadboards: 1

parts:
  U1 = NodeMCU V1.0
  R1 = Photocell (LDR) [package=THT]
  R2 = Resistor [tolerance=±5% resistance=10k package="0603 [SMD]"]
  LED1 = LED - 3mm [color="Red (633nm)" package="3 mm [THT]"]
  R3 = Resistor [tolerance=±5% resistance=330 package="0603 [SMD]"]
  PIR1 = PIR sensor

nets:
  N1: U1.D4, PIR1.SIG
  3V3: U1.3V3, R1.pin_1, PIR1.VDD
  GND: U1.GND, R2.Pin_1, R3.Pin_1, PIR1.GND
  N2: U1.D5, LED1.anode
  N3: U1.A0, R1.pin_0, R2.Pin_0
  N4: LED1.cathode, R3.Pin_0

custom parts:
  NodeMCU V1.0: ESP8266 based NodeMCU
